# Fritzing sketch connections (saved by Fritzing 0.9.9b)
breadboards: 1

parts:
  Adafruit_HUZZAH_ESP8266_Breakout1 = Adafruit HUZZAH ESP8266 Breakout [part_number=2471]
  Part1 = BME280 Breakout
  Grove1 = Grove OLED 128x96
  Power_plug1 = Power plug

nets:
  GND: Adafruit_HUZZAH_ESP8266_Breakout1.GND, Power_plug1.GND
  N1: Adafruit_HUZZAH_ESP8266_Breakout1.V+, Power_plug1.VCC
  N2: Adafruit_HUZZAH_ESP8266_Breakout1.#5, Part1.SCK/SCL, Grove1.SCL
  N3: Adafruit_HUZZAH_ESP8266_Breakout1.#4, Part1.SDI/SDA, Grove1.SDA
  GND_2: Part1.GND, Grove1.GND
  3.3V: Part1.3.3V, Grove1.VCC
